// Logisim project Final_Circuit_Project.circ as structural Verilog: 1 circuit, main circuit main
module main (
  input  A,
  input  B,
  input  C,
  input  D,
  input  E
);

  wire _7_2_out, _7_3_out, _7_4_out, _7_5_out, _7_6_out, _7_7_out, _7_8_out, _7_9_out, _7_10_out, _7_11_out,
       _7_12_out, _7_13_out, _7_14_out, _7_15_out, _7_16_out, _7_17_out, _7_18_out, _7_19_out, _7_20_out,
       _7_21_out, _7_22_out, _7_23_out, _7_24_out, _7_out, _14_2_out, _14_out, not_1_out, not_2_out,
       not_3_out, not_4_out, not_5_out, not_6_out, not_7_out, not_8_out, not_9_out;

  not not_1 (not_1_out, D);
  not not_2 (not_2_out, E);
  or _14 (_14_out, C, D, E);
  or _7 (_7_out, D, E);
  and _7_2 (_7_2_out, B, _14_out);
  not not_3 (not_3_out, C);
  not not_4 (not_4_out, D);
  not not_5 (not_5_out, E);
  not not_6 (not_6_out, D);
  not not_7 (not_7_out, B);
  not not_8 (not_8_out, E);
  and _7_3 (_7_3_out, not_1_out, not_2_out);
  and _14_2 (_14_2_out, not_3_out, not_4_out, not_5_out);
  and _7_4 (_7_4_out, C, E);
  and _7_5 (_7_5_out, A, _7_out);
  or _7_6 (_7_6_out, not_6_out, E);
  and _7_7 (_7_7_out, D, not_8_out);
  and _7_8 (_7_8_out, B, C);
  or _7_9 (_7_9_out, A, _7_2_out);
  or _7_10 (_7_10_out, not_7_out, _7_7_out);
  or _7_11 (_7_11_out, _14_2_out, _7_4_out);
  and _7_12 (_7_12_out, A, _7_6_out);
  and _7_13 (_7_13_out, C, _7_10_out);
  not not_9 (not_9_out, A);
  LED led_1 (.in(_7_9_out));
  and _7_14 (_7_14_out, B, _7_11_out);
  and _7_15 (_7_15_out, not_9_out, not_7_out);
  or _7_16 (_7_16_out, _7_8_out, A);
  or _7_17 (_7_17_out, _7_14_out, _7_5_out);
  or _7_18 (_7_18_out, _7_12_out, _7_13_out);
  or _7_19 (_7_19_out, _7_15_out, E);
  and _7_20 (_7_20_out, _7_3_out, _7_16_out);
  LED led_2 (.in(_7_17_out));
  or _7_21 (_7_21_out, B, C);
  LED led_3 (.in(_7_18_out));
  and _7_22 (_7_22_out, _7_19_out, D);
  or _7_23 (_7_23_out, _7_22_out, _7_20_out);
  and _7_24 (_7_24_out, A, _7_21_out);
  LED led_4 (.in(_7_24_out));
  LED led_5 (.in(_7_23_out));

  // Notes on the sheet:
  //   E+D+C
  //             E+D
  //   2
  //   2
  //   Numbers show how may transistors inside each gate
  //   2
  //   2
  //   2
  //                     D!*E!
  //                  B*(E+D+C)
  //   2
  //   2
  //   2
  //                       C!*D!*E!
  //        C*E
  //                A*(E+D)
  //                    E+D!
  //                D*E!
  //             B*C
  //                  A+B*(E+D+C)
  //   B!+D*E!
  //                          C!*D!*E!+C*E
  //             A*(E+D!)
  //   2
  //                           B*(C*E+C!*D!*E!!)
  //                      C*(B!+D*E!)
  //   A!*B!
  //             B*C+A
  //   Q
  //   A*(E+D!)+C*(B!+D*E!)
  //                    D!*E!*(B*C+A)
  //                                 A*(E+D)+B*(C*E*+C!*D!*E!)
  //   E+A!*B!
  //   D*(E+A!*B!)
  //                 B+C
  //   R
  //   S
  //                                                           D*(E+A!*B!)+D!*E!*(B*C+A)
  //                     A*(B+C)
  //   U
  //   T
endmodule
