// Logisim project Final_Circuit_Project_Improved.circ as structural Verilog: 1 circuit, main circuit main
module main (
  input  A,
  input  B,
  input  C,
  input  D,
  input  E
);

  wire _2_out, _7_2_out, _7_3_out, _7_4_out, _7_5_out, _7_6_out, _7_7_out, _7_8_out, _7_9_out, _7_10_out,
       _7_11_out, _7_12_out, _7_13_out, _7_14_out, _7_15_out, _7_16_out, _7_17_out, _7_18_out, _7_19_out,
       _7_20_out, _7_21_out, _7_22_out, _7_23_out, _7_24_out, _7_out, _14_2_out, _14_out, not_1_out,
       not_2_out, not_3_out, not_4_out;

  not not_1 (not_1_out, E);
  not not_2 (not_2_out, C);
  not not_3 (not_3_out, A);
  not _2 (_2_out, D);
  or _14 (_14_out, E, D, C);
  or _7 (_7_out, D, E);
  and _7_2 (_7_2_out, C, E);
  and _14_2 (_14_2_out, not_1_out, _2_out, not_2_out);
  or _7_3 (_7_3_out, E, _2_out);
  not not_4 (not_4_out, B);
  and _7_4 (_7_4_out, B, C);
  and _7_5 (_7_5_out, D, not_1_out);
  and _7_6 (_7_6_out, not_3_out, not_4_out);
  or _7_7 (_7_7_out, B, C);
  and _7_8 (_7_8_out, _14_out, B);
  or _7_9 (_7_9_out, _7_2_out, _14_2_out);
  or _7_10 (_7_10_out, _7_6_out, E);
  or _7_11 (_7_11_out, _7_4_out, A);
  and _7_12 (_7_12_out, not_1_out, _2_out);
  and _7_13 (_7_13_out, _7_out, A);
  and _7_14 (_7_14_out, _7_3_out, A);
  and _7_15 (_7_15_out, _7_7_out, A);
  or _7_16 (_7_16_out, _7_8_out, A);
  or _7_17 (_7_17_out, _7_5_out, not_4_out);
  and _7_18 (_7_18_out, _7_10_out, D);
  and _7_19 (_7_19_out, _7_11_out, _7_12_out);
  LED led_1 (.in(_7_16_out));
  and _7_20 (_7_20_out, _7_9_out, B);
  LED led_2 (.in(_7_15_out));
  or _7_21 (_7_21_out, _7_13_out, _7_20_out);
  and _7_22 (_7_22_out, _7_17_out, C);
  or _7_23 (_7_23_out, _7_18_out, _7_19_out);
  LED led_3 (.in(_7_21_out));
  or _7_24 (_7_24_out, _7_14_out, _7_22_out);
  LED led_4 (.in(_7_24_out));
  LED led_5 (.in(_7_23_out));

  // Notes on the sheet:
  //   Numbers show how many transistors inside each gate
  //   2
  //   2
  //   2
  //   E+D+C
  //               E+D
  //   2
  //                 B*C
  //           C*E
  //             (C!*D!*E!)
  //                E+D!
  //              A!*B!
  //              B+C
  //        B*(E+D+C)
  //               D*E!
  //                 D!*E!
  //                C*E+C!*D!*E!
  //                  A*(E+D!)
  //   E+A!*B!
  //            B*C+A
  //                   A*(B+C)
  //                A*(E+D)
  //   B!+D*E!
  //                 D*(E+A!*B!)
  //   A+B*(E+D+C)
  //               B*(C*E+C!*D!*E!)
  //                         D!*E!*(B*C+A)
  //   Q
  //                      C*(B!+D*E!)
  //          A*(E+D)+B*(C*E+C!*D!*E!)
  //                         D*(E+A!*B!)+D!*E!*(B*C+A)
  //      U
  //   R
  //                 A*(E+D!)+C*(B!+D*E!)
  //   S
  //           T 
endmodule
